// Logisim project main.circ as structural Verilog: 11 circuits, main circuit main
module main (
  input  [3:0] in_1,
  output [3:0] out_2
);

  wire memory_address_register_1_p3, out_reg_1_p2;
  wire [1:0] instruction_register_1_p1, memory_address_register_1_p1, out_reg_1_p3, undriven_2;
  wire [2:0] accumulator_1_p3, undriven, undriven_3;
  wire [3:0] accumulator_1_p2, binary_to_bcd_converter_1_p2, binary_to_bcd_converter_1_p3, reg_b_1_dout;

  // memory_address_register memory_address_register_1: pin names not known; wires that end beside it: memory_address_register_1_p1[0], memory_address_register_1_p1[1], memory_address_register_1_p3, out_2, in_1
  program_counter program_counter_1 (
    .initINC(undriven[0]), .cJUMP(undriven[1]), .instADDR(in_1), .clk(memory_address_register_1_p3),
    .reset(undriven[2]), .incOUT(in_1));
  // instruction_register instruction_register_1: pin names not known; wires that end beside it: instruction_register_1_p1[0], instruction_register_1_p1[1], memory_address_register_1_p3, in_1, in_1
  // accumulator accumulator_1: pin names not known; wires that end beside it: in_1, accumulator_1_p2, accumulator_1_p3[0], accumulator_1_p3[1], accumulator_1_p3[2], memory_address_register_1_p3
  adder_subtractor adder_subtractor_1 (
    .cSUB(undriven_2[0]), .B(reg_b_1_dout), .A(accumulator_1_p2), .enAS(undriven_2[1]), .Result(in_1));  // open: fZERO, fNEG
  reg_b reg_b_1 (
    .dIN(in_1), .LOAD(undriven_3[0]), .clk(memory_address_register_1_p3), .reset(undriven_3[2]),
    .STRE(undriven_3[1]), .dOUT(reg_b_1_dout));
  // out_reg out_reg_1: pin names not known; wires that end beside it: in_1, out_reg_1_p2, out_reg_1_p3[0], out_reg_1_p3[1], memory_address_register_1_p3
  Hex_Digit_Display hex_digit_display_1 (.value(binary_to_bcd_converter_1_p2));  // open: dp
  Hex_Digit_Display hex_digit_display_2 (.value(binary_to_bcd_converter_1_p3));  // open: dp
  // Binary_to_BCD_converter #(.binvalue(4)) binary_to_bcd_converter_1: pin names not known; wires that end beside it: out_reg_1_p2, binary_to_bcd_converter_1_p2, binary_to_bcd_converter_1_p3
endmodule

module adder_subtractor (
  input  cSUB,
  input  [3:0] B,
  input  [3:0] A,
  input  enAS,
  output [3:0] Result,
  output fZERO,
  output fNEG
);

  wire full_adder_1_cout, full_adder_2_cout, full_adder_3_cout, xor_1_out, xor_2_out, xor_3_out, xor_4_out;
  wire [2:0] full_adder_1_s;

  xor xor_1 (xor_1_out, B[3], cSUB);
  xor xor_2 (xor_2_out, B[2], cSUB);
  xor xor_3 (xor_3_out, B[1], cSUB);
  xor xor_4 (xor_4_out, B[0], cSUB);
  full_adder full_adder_1 (.A(A[0]), .B(xor_4_out), .C(cSUB), .S(full_adder_1_s[0]), .Cout(full_adder_1_cout));
  full_adder full_adder_2 (
    .A(A[1]), .B(xor_3_out), .C(full_adder_1_cout), .S(full_adder_1_s[1]), .Cout(full_adder_2_cout));
  full_adder full_adder_3 (
    .A(A[2]), .B(xor_2_out), .C(full_adder_2_cout), .S(full_adder_1_s[2]), .Cout(full_adder_3_cout));
  full_adder full_adder_4 (.A(A[3]), .B(xor_1_out), .C(full_adder_3_cout), .S(fNEG));  // open: Cout
  assign Result = enAS ? {fNEG, full_adder_1_s} : 4'bz;  // Controlled_Buffer controlled_buffer_1
  nor nor_1 (fZERO, full_adder_1_s[0], full_adder_1_s[1], full_adder_1_s[2], fNEG);
endmodule

module full_adder (
  input  A,
  input  B,
  input  C,
  output S,
  output Cout
);

  wire and_1_out, and_2_out, xor_1_out;

  xor xor_1 (xor_1_out, A, B);
  and and_1 (and_1_out, A, B);
  xor xor_2 (S, xor_1_out, C);
  and and_2 (and_2_out, xor_1_out, C);
  or or_1 (Cout, and_2_out, and_1_out);
endmodule

module program_counter (
  input  initINC,
  input  cJUMP,
  input  [3:0] instADDR,
  input  clk,
  input  reset,
  output [3:0] incOUT
);

  wire half_adder_1_cout, half_adder_1_sum, half_adder_2_cout, half_adder_2_sum, half_adder_3_cout,
       half_adder_3_sum, half_adder_4_cout, half_adder_4_sum, multiplexer_1_out, multiplexer_2_out,
       multiplexer_3_out, multiplexer_4_out, not_1_out;

  not not_1 (not_1_out, clk);
  half_adder half_adder_1 (.A(incOUT[3]), .B(half_adder_2_cout), .Sum(half_adder_1_sum), .Cout(half_adder_1_cout));
  D_Flip_Flop d_ff_1 (.D(multiplexer_1_out), .clk(not_1_out), .Q(incOUT[3]), .reset(reset));  // open: Qn, preset
  Multiplexer multiplexer_1 (.in0(half_adder_1_sum), .in1(instADDR[3]), .out(multiplexer_1_out), .sel(cJUMP));
  Multiplexer multiplexer_2 (.in0(half_adder_2_sum), .in1(instADDR[2]), .out(multiplexer_2_out), .sel(cJUMP));
  half_adder half_adder_2 (.A(incOUT[2]), .B(half_adder_3_cout), .Sum(half_adder_2_sum), .Cout(half_adder_2_cout));
  D_Flip_Flop d_ff_2 (.D(multiplexer_2_out), .clk(not_1_out), .Q(incOUT[2]), .reset(reset));  // open: Qn, preset
  half_adder half_adder_3 (.A(incOUT[1]), .B(half_adder_4_cout), .Sum(half_adder_3_sum), .Cout(half_adder_3_cout));
  D_Flip_Flop d_ff_3 (.D(multiplexer_3_out), .clk(not_1_out), .Q(incOUT[1]), .reset(reset));  // open: Qn, preset
  Multiplexer multiplexer_3 (.in0(half_adder_3_sum), .in1(instADDR[1]), .out(multiplexer_3_out), .sel(cJUMP));
  half_adder half_adder_4 (.A(incOUT[0]), .B(initINC), .Sum(half_adder_4_sum), .Cout(half_adder_4_cout));
  D_Flip_Flop d_ff_4 (.D(multiplexer_4_out), .clk(not_1_out), .Q(incOUT[0]), .reset(reset));  // open: Qn, preset
  Multiplexer multiplexer_4 (.in0(half_adder_4_sum), .in1(instADDR[0]), .out(multiplexer_4_out), .sel(cJUMP));
  // also tied to GND on the sheet: half_adder_1_cout

  // Notes on the sheet:
  //   Incrementation: Addition of previous state
  //   Choosing of Address
endmodule

module half_adder (
  input  A,
  input  B,
  output Sum,
  output Cout
);

  xor xor_1 (Sum, A, B);
  and and_1 (Cout, A, B);
endmodule

module accumulator (
  input  [7:0] dINBUS,
  input  load,
  input  clk,
  input  reset,
  input  store,
  output [7:0] dOUTBUS,
  output [7:0] dOUTADDSUB
);

  wire [7:0] controlled_buffer_1_out;

  assign controlled_buffer_1_out = load ? dINBUS : 8'bz;  // Controlled_Buffer controlled_buffer_1
  D_Flip_Flop d_ff_1 (.D(controlled_buffer_1_out[0]), .clk(clk), .Q(dOUTADDSUB[0]), .reset(reset));  // open: Qn, preset
  D_Flip_Flop d_ff_2 (.D(controlled_buffer_1_out[1]), .clk(clk), .Q(dOUTADDSUB[1]), .reset(reset));  // open: Qn, preset
  D_Flip_Flop d_ff_3 (.D(controlled_buffer_1_out[2]), .clk(clk), .Q(dOUTADDSUB[2]), .reset(reset));  // open: Qn, preset
  D_Flip_Flop d_ff_4 (.D(controlled_buffer_1_out[3]), .clk(clk), .Q(dOUTADDSUB[3]), .reset(reset));  // open: Qn, preset
  D_Flip_Flop d_ff_5 (.D(controlled_buffer_1_out[4]), .clk(clk), .Q(dOUTADDSUB[4]), .reset(reset));  // open: Qn, preset
  D_Flip_Flop d_ff_6 (.D(controlled_buffer_1_out[5]), .clk(clk), .Q(dOUTADDSUB[5]), .reset(reset));  // open: Qn, preset
  D_Flip_Flop d_ff_7 (.D(controlled_buffer_1_out[6]), .clk(clk), .Q(dOUTADDSUB[6]), .reset(reset));  // open: Qn, preset
  D_Flip_Flop d_ff_8 (.D(controlled_buffer_1_out[7]), .clk(clk), .Q(dOUTADDSUB[7]), .reset(reset));  // open: Qn, preset
  assign dOUTBUS = store ? dOUTADDSUB : 8'bz;  // Controlled_Buffer controlled_buffer_2
endmodule

module instruction_register (
  input  [7:0] iBUS,
  input  clkFETCH,
  input  clk,
  input  reset,
  output [7:0] iCTRL
);

  wire [7:0] controlled_buffer_1_out;

  assign controlled_buffer_1_out = clkFETCH ? iBUS : 8'bz;  // Controlled_Buffer controlled_buffer_1
  D_Flip_Flop d_ff_1 (.D(controlled_buffer_1_out[0]), .clk(clk), .Q(iCTRL[0]), .reset(reset));  // open: Qn, preset
  D_Flip_Flop d_ff_2 (.D(controlled_buffer_1_out[1]), .clk(clk), .Q(iCTRL[1]), .reset(reset));  // open: Qn, preset
  D_Flip_Flop d_ff_3 (.D(controlled_buffer_1_out[2]), .clk(clk), .Q(iCTRL[2]), .reset(reset));  // open: Qn, preset
  D_Flip_Flop d_ff_4 (.D(controlled_buffer_1_out[3]), .clk(clk), .Q(iCTRL[3]), .reset(reset));  // open: Qn, preset
  D_Flip_Flop d_ff_5 (.D(controlled_buffer_1_out[4]), .clk(clk), .Q(iCTRL[4]), .reset(reset));  // open: Qn, preset
  D_Flip_Flop d_ff_6 (.D(controlled_buffer_1_out[5]), .clk(clk), .Q(iCTRL[5]), .reset(reset));  // open: Qn, preset
  D_Flip_Flop d_ff_7 (.D(controlled_buffer_1_out[6]), .clk(clk), .Q(iCTRL[6]), .reset(reset));  // open: Qn, preset
  D_Flip_Flop d_ff_8 (.D(controlled_buffer_1_out[7]), .clk(clk), .Q(iCTRL[7]), .reset(reset));  // open: Qn, preset
endmodule

module memory_address_register (
  input  [7:0] dBUS,
  input  enMAR,
  input  clk,
  input  reset,
  output [7:0] dRAM
);

  wire [7:0] controlled_buffer_1_out;

  assign controlled_buffer_1_out = enMAR ? dBUS : 8'bz;  // Controlled_Buffer controlled_buffer_1
  D_Flip_Flop d_ff_1 (.D(controlled_buffer_1_out[0]), .clk(clk), .Q(dRAM[0]), .reset(reset));  // open: Qn, preset
  D_Flip_Flop d_ff_2 (.D(controlled_buffer_1_out[1]), .clk(clk), .Q(dRAM[1]), .reset(reset));  // open: Qn, preset
  D_Flip_Flop d_ff_3 (.D(controlled_buffer_1_out[2]), .clk(clk), .Q(dRAM[2]), .reset(reset));  // open: Qn, preset
  D_Flip_Flop d_ff_4 (.D(controlled_buffer_1_out[3]), .clk(clk), .Q(dRAM[3]), .reset(reset));  // open: Qn, preset
  D_Flip_Flop d_ff_5 (.D(controlled_buffer_1_out[4]), .clk(clk), .Q(dRAM[4]), .reset(reset));  // open: Qn, preset
  D_Flip_Flop d_ff_6 (.D(controlled_buffer_1_out[5]), .clk(clk), .Q(dRAM[5]), .reset(reset));  // open: Qn, preset
  D_Flip_Flop d_ff_7 (.D(controlled_buffer_1_out[6]), .clk(clk), .Q(dRAM[6]), .reset(reset));  // open: Qn, preset
  D_Flip_Flop d_ff_8 (.D(controlled_buffer_1_out[7]), .clk(clk), .Q(dRAM[7]), .reset(reset));  // open: Qn, preset
endmodule

module reg_b (
  input  [3:0] dIN,
  input  LOAD,
  input  clk,
  input  reset,
  input  STRE,
  output [3:0] dOUT
);

  wire [3:0] controlled_buffer_1_out, d_ff_1_q;

  assign controlled_buffer_1_out = LOAD ? dIN : 4'bz;  // Controlled_Buffer controlled_buffer_1
  D_Flip_Flop d_ff_1 (.D(controlled_buffer_1_out[0]), .clk(clk), .Q(d_ff_1_q[0]), .reset(reset));  // open: Qn, preset
  D_Flip_Flop d_ff_2 (.D(controlled_buffer_1_out[1]), .clk(clk), .Q(d_ff_1_q[1]), .reset(reset));  // open: Qn, preset
  D_Flip_Flop d_ff_3 (.D(controlled_buffer_1_out[2]), .clk(clk), .Q(d_ff_1_q[2]), .reset(reset));  // open: Qn, preset
  D_Flip_Flop d_ff_4 (.D(controlled_buffer_1_out[3]), .clk(clk), .Q(d_ff_1_q[3]), .reset(reset));  // open: Qn, preset
  assign dOUT = STRE ? d_ff_1_q : 4'bz;  // Controlled_Buffer controlled_buffer_2
endmodule

module out_reg (
  input  [7:0] dIN,
  input  outLOAD,
  input  clk,
  input  reset,
  output [7:0] dOUT
);

  wire [7:0] controlled_buffer_1_out;

  assign controlled_buffer_1_out = outLOAD ? dIN : 8'bz;  // Controlled_Buffer controlled_buffer_1
  D_Flip_Flop d_ff_1 (.D(controlled_buffer_1_out[0]), .clk(clk), .Q(dOUT[0]), .reset(reset));  // open: Qn, preset
  D_Flip_Flop d_ff_2 (.D(controlled_buffer_1_out[1]), .clk(clk), .Q(dOUT[1]), .reset(reset));  // open: Qn, preset
  D_Flip_Flop d_ff_3 (.D(controlled_buffer_1_out[2]), .clk(clk), .Q(dOUT[2]), .reset(reset));  // open: Qn, preset
  D_Flip_Flop d_ff_4 (.D(controlled_buffer_1_out[3]), .clk(clk), .Q(dOUT[3]), .reset(reset));  // open: Qn, preset
  D_Flip_Flop d_ff_5 (.D(controlled_buffer_1_out[4]), .clk(clk), .Q(dOUT[4]), .reset(reset));  // open: Qn, preset
  D_Flip_Flop d_ff_6 (.D(controlled_buffer_1_out[5]), .clk(clk), .Q(dOUT[5]), .reset(reset));  // open: Qn, preset
  D_Flip_Flop d_ff_7 (.D(controlled_buffer_1_out[6]), .clk(clk), .Q(dOUT[6]), .reset(reset));  // open: Qn, preset
  D_Flip_Flop d_ff_8 (.D(controlled_buffer_1_out[7]), .clk(clk), .Q(dOUT[7]), .reset(reset));  // open: Qn, preset
endmodule

module controller (
  input  [7:0] in_1,
  output [2:0] out_2,
  output [2:0] out_3,
  output [1:0] out_4,
  output [1:0] out_5,
  output [1:0] out_6,
  output [2:0] out_7,
  output [1:0] out_8,
  output [1:0] out_9
);

  // NAND_Gate nand_1 is placed but not wired
endmodule
